# Fritzing sketch arduino_button (saved by Fritzing 0.9.0b)

parts:
  Part3 = Arduino Micro (Rev3)
  S1 = Round Pushbutton
  R2 = Resistor [tolerance=±5% resistance=10k package=THT]

nets:
  N1: Part3.GND, R2.Pin_1
  N2: Part3.D7, S1.leg0, R2.Pin_0
  N3: Part3.5V, S1.leg1
