# Fritzing sketch arduino_nano_light_sensor (saved by Fritzing 0.9.2b)
breadboards: 1

parts:
  R1 = PHOTOCELL [package=photocell-kit]
  R2 = Resistor [tolerance=±5% resistance=220 package=THT]
  Part3 = Arduino Micro (Rev3)

nets:
  N1: R1.P$1, R2.Pin_0, Part3.A5
  N2: R1.P$2, Part3.5V
  N3: R2.Pin_1, Part3.GND
